# Fritzing sketch Interruptor Conectado Modulo 01 (saved by Fritzing 0.9.3b)
breadboards: 1

parts:
  U1 = 4-Channel 5v Relay Shield [package=relay-4ch5v10a]
  U2 = NodeMCU V1.0
  PIR1 = PIR sensor
  T1 = LM35 Temperature Sensor [package="TO92 [THT]"]  # not connected
  S1 = SPST Switch [package=switch-spdt]
  S2 = SPST Switch [package=switch-spdt]
  S3 = SPST Switch [package=switch-spdt]
  S4 = SPST Switch [package=switch-spdt]

nets:
  VCC: U1.VCC, U2.Vin, PIR1.VDD
  GND: U1.GND, U2.GND, PIR1.GND, S1.S, S2.S, S3.S, S4.S
  N1: U1.IN1, U2.D5
  N2: U1.IN2, U2.D6
  N3: U1.K1-On, U1.K2-Off, U1.K2-On, U1.K3-In, U1.K3-On
  N4: U1.IN4, U2.RX
  N5: U1.IN3, U2.D7
  N6: U2.D0, PIR1.SIG
  N7: U2.D1, S1.P
  N8: U2.D2, S2.P
  N9: U2.D3, S3.P
  N10: U2.D4, S4.P

custom parts:
  4-Channel 5v Relay Shield: 4 Channel 5v Relay Shield w. 2x SPD-06VDC-SD-C
  NodeMCU V1.0: ESP8266 based NodeMCU
